// Logisim project NanoSwitch16.circ as structural Verilog: 2 circuits, main circuit main
module main (
  input  [3:0] page,
  output [3:0] out_2,
  output _0000,
  output _0001,
  output _0010,
  output _0011,
  output _0100,
  output _0101,
  output _0110,
  output _0111,
  output _1000,
  output _1001,
  output _1010,
  output _1011,
  output _1100,
  output _1101,
  output _1110,
  output _1111
);

  wire adder_1_y, adder_2_x, adder_2_y, adder_3_x, adder_3_y, adder_4_x, adder_4_y, clock_1_out, d_ff_5_q,
       d_ff_6_q, d_ff_7_q, d_ff_8_q, not_1_out, not_2_out, not_3_out, not_4_out, not_5_out;
  wire [7:0] ram_1_dout;

  Clock clock_1 (.out(clock_1_out));
  not not_1 (not_1_out, clock_1_out);
  D_Flip_Flop d_ff_1 (.D(d_ff_5_q), .clk(not_1_out), .Q(out_2[3]));  // open: Qn, preset, reset
  D_Flip_Flop d_ff_2 (.D(d_ff_6_q), .clk(not_1_out), .Q(out_2[2]));  // open: Qn, preset, reset
  D_Flip_Flop d_ff_3 (.D(d_ff_7_q), .clk(not_1_out), .Q(out_2[1]));  // open: Qn, preset, reset
  D_Flip_Flop d_ff_4 (.D(d_ff_8_q), .clk(not_1_out), .Q(out_2[0]));  // open: Qn, preset, reset
  RAM ram_1 (.addr({page, out_2}), .oe(1'b1), .clk(clock_1_out), .dout(ram_1_dout));  // open: we, din
  adder adder_1 (.a(out_2[3]), .b(adder_2_x), .y(adder_1_y));  // open: x
  adder adder_2 (.a(out_2[2]), .b(adder_3_x), .x(adder_2_x), .y(adder_2_y));
  adder adder_3 (.a(out_2[1]), .b(adder_4_x), .x(adder_3_x), .y(adder_3_y));
  adder adder_4 (.a(out_2[0]), .b(1'b1), .x(adder_4_x), .y(adder_4_y));
  D_Flip_Flop d_ff_5 (.D(adder_1_y), .clk(clock_1_out), .Q(d_ff_5_q));  // open: Qn, preset, reset
  D_Flip_Flop d_ff_6 (.D(adder_2_y), .clk(clock_1_out), .Q(d_ff_6_q));  // open: Qn, preset, reset
  D_Flip_Flop d_ff_7 (.D(adder_3_y), .clk(clock_1_out), .Q(d_ff_7_q));  // open: Qn, preset, reset
  D_Flip_Flop d_ff_8 (.D(adder_4_y), .clk(clock_1_out), .Q(d_ff_8_q));  // open: Qn, preset, reset
  not not_2 (not_2_out, ram_1_dout[3]);
  not not_3 (not_3_out, ram_1_dout[2]);
  not not_4 (not_4_out, ram_1_dout[1]);
  not not_5 (not_5_out, ram_1_dout[0]);
  and and_1 (_0000, not_5_out, not_4_out, not_3_out, not_2_out);
  and and_2 (_0001, ram_1_dout[0], not_4_out, not_3_out, not_2_out);
  and and_3 (_0010, not_5_out, ram_1_dout[1], not_3_out, not_2_out);
  and and_4 (_0011, ram_1_dout[0], ram_1_dout[1], not_3_out, not_2_out);
  and and_5 (_0100, not_5_out, not_4_out, ram_1_dout[2], not_2_out);
  and and_6 (_0101, ram_1_dout[0], not_4_out, ram_1_dout[2], not_2_out);
  and and_7 (_0110, not_5_out, ram_1_dout[1], ram_1_dout[2], not_2_out);
  and and_8 (_0111, ram_1_dout[0], ram_1_dout[1], ram_1_dout[2], not_2_out);
  and and_9 (_1000, not_5_out, not_4_out, not_3_out, ram_1_dout[3]);
  and and_10 (_1001, ram_1_dout[0], not_4_out, not_3_out, ram_1_dout[3]);
  and and_11 (_1010, not_5_out, ram_1_dout[1], not_3_out, ram_1_dout[3]);
  and and_12 (_1011, ram_1_dout[0], ram_1_dout[1], not_3_out, ram_1_dout[3]);
  and and_13 (_1100, not_5_out, not_4_out, ram_1_dout[2], ram_1_dout[3]);
  and and_14 (_1101, ram_1_dout[0], not_4_out, ram_1_dout[2], ram_1_dout[3]);
  and and_15 (_1110, not_5_out, ram_1_dout[1], ram_1_dout[2], ram_1_dout[3]);
  and and_16 (_1111, ram_1_dout[0], ram_1_dout[1], ram_1_dout[2], ram_1_dout[3]);
endmodule

module adder (
  input  a,
  input  b,
  output x,
  output y
);

  wire and_2_out, and_3_out, not_1_out, not_2_out;

  not not_1 (not_1_out, a);
  not not_2 (not_2_out, b);
  and and_1 (x, a, b);
  and and_2 (and_2_out, a, not_2_out);
  and and_3 (and_3_out, not_1_out, b);
  or or_1 (y, and_2_out, and_3_out);
endmodule
